# Fritzing sketch sematikcizim (saved by Fritzing 0.9.3b)
breadboards: 1

parts:
  Parça1 = MQ-4
  Parça2 = Arduino Uno (Rev3)
  SG1 = Buzzer 12mm [package=buzzer-ccv]
  LCD1 = LCD screen

nets:
  N1: Parça1.VCC, Parça2.A0
  GND: Parça1.GND, Parça2.VIN
  N2: Parça1.DO, Parça2.GND, SG1.1
  N3: Parça2.D9_PWM, SG1.2
  N4: Parça2.D11_PWM/MOSI, LCD1.E
  N5: Parça2.D12/MISO, LCD1.RS
  N6: Parça2.D2, LCD1.DB7
  N7: Parça2.D3_PWM, LCD1.DB6
  N8: Parça2.D4, LCD1.DB5
  N9: Parça2.D5_PWM, LCD1.DB4
  N10: LCD1.VSS, LCD1.V0, LCD1.R/W, LCD1.LED-
  N11: LCD1.VDD, LCD1.LED+
